# Fritzing sketch esp32-devkitc-wiring (saved by Fritzing 0.9.4)

parts:
  MH-ET_LIVE_ESP32_DEVKIT1 = MH-ET LIVE ESP32 DEVKIT 38 pins
  J2 = Generic shrouded header - 8 pins [form="♂ (shrouded male)" package=THT]
  J3 = Generic shrouded header - 8 pins [form="♂ (shrouded male)" package=THT]
  J4 = Generic shrouded header - 8 pins [form="♂ (shrouded male)" package=THT]
  J5 = Generic shrouded header - 8 pins [form="♂ (shrouded male)" package=THT]
  J6 = Generic shrouded header - 8 pins [form="♂ (shrouded male)" package=THT]
  J7 = Generic shrouded header - 8 pins [form="♂ (shrouded male)" package=THT]

nets:
  N1: MH-ET_LIVE_ESP32_DEVKIT1.GND, J6.D2, J6.OE, J6.A0, J6.CLK, J6.NC, J6.A1, J6.LAT, J6.D1
  N2: MH-ET_LIVE_ESP32_DEVKIT1.IO22, J2.CLK, J2.NC
  N3: MH-ET_LIVE_ESP32_DEVKIT1.IO21, J2.LAT
  N4: MH-ET_LIVE_ESP32_DEVKIT1.IO19, J2.OE
  N5: MH-ET_LIVE_ESP32_DEVKIT1.IO18, J2.A1, J2.D1
  N6: MH-ET_LIVE_ESP32_DEVKIT1.IO5, J2.D2, J2.A0
  N7: MH-ET_LIVE_ESP32_DEVKIT1.IO17, J3.D1
  N8: MH-ET_LIVE_ESP32_DEVKIT1.IO16, J3.D2
  N9: MH-ET_LIVE_ESP32_DEVKIT1.IO4, J4.D1
  N10: MH-ET_LIVE_ESP32_DEVKIT1.IO0, J4.D2
  N11: MH-ET_LIVE_ESP32_DEVKIT1.IO2, J5.D1
  N12: MH-ET_LIVE_ESP32_DEVKIT1.IO15, J5.D2
  N13: J7.D2, J7.OE, J7.A0, J7.CLK, J7.NC, J7.A1, J7.LAT, J7.D1

notes:
  Panel 1 Data (Top)
  Panel 2 Data
  Panel 3 Data
  Panel 4 Data (Bottom)
  Panel GND
  +5V
  Pins 3-7 as per Panel 1
  Panel +5V
  ESP32 DevKitC/NodeMCU

custom parts:
  MH-ET LIVE ESP32 DEVKIT 38 pins: http://mh.nodebb.com/topic/2/mh-et-live-esp32-devkit
  Generic shrouded header - 8 pins: Generic shrouded header
